# Fritzing sketch schematic (saved by Fritzing 0.9.6b)
breadboards: 1

parts:
  U1 = mystery part, 6 pins [chip_label="6 "]
  U2 = mystery part, 4 pins [chip_label=?]
  U3 = mystery part, 2 pins [chip_label=?]  # not connected
  U4 = mystery part, 2 pins [chip_label=?]  # not connected
  U5 = mystery part, 2 pins [chip_label=?]  # not connected
  U6 = mystery part, 2 pins [chip_label=?]
  U7 = mystery part, 2 pins [chip_label=?]
  U8 = mystery part, 4 pins [chip_label=?]
  U9 = mystery part, 3 pins [chip_label=?]
  Raspberry_Pi_1 = Raspberry Pi 3 [part_number=RPI-3-V1.2]

nets:
  N1: U1.pin4, U9.pin2, Raspberry_Pi_1.GND
  N2: U1.pin6, U9.pin1
  N3: U2.pin1, U7.pin2
  N4: U2.pin2, U6.pin1
  N5: U2.pin3, U7.pin1
  N6: U2.pin4, U6.pin2
  N7: U8.pin1, Raspberry_Pi_1.ID_SC
  N8: U8.pin2, Raspberry_Pi_1.ID_SD
  N9: U8.pin3, Raspberry_Pi_1.GPIO2
  N10: U8.pin4, Raspberry_Pi_1.GPIO3
