# Fritzing sketch motor-test-tail-foreward (saved by Fritzing 0.9.6b)
breadboards: 1

parts:
  U1 = mystery part, 6 pins [chip_label="6 "]
  U2 = mystery part, 4 pins [chip_label=?]
  U3 = mystery part, 2 pins [chip_label=?]  # not connected
  U4 = mystery part, 2 pins [chip_label=?]  # not connected
  U5 = mystery part, 2 pins [chip_label=?]  # not connected

nets:
  N1: U1.pin4, U2.pin4
  N2: U1.pin6, U2.pin2, U2.pin3
